// Logisim project branch-comp.circ as structural Verilog: 1 circuit, main circuit branch_comp
module branch_comp (
  input  [31:0] BrData1,
  input  [31:0] BrData2,
  input  BrUn,
  output BrEq,
  output BrLt
);

  wire EqS, EqU, LTS, LTU;

  Comparator #(.mode("unsigned"), .width(32)) comparator_1 (.a(BrData1), .b(BrData2), .eq(EqU), .lt(LTU));  // open: gt
  Comparator #(.width(32)) comparator_2 (.a(BrData1), .b(BrData2), .eq(EqS), .lt(LTS));  // open: gt
  Multiplexer multiplexer_1 (.in0(EqU), .in1(EqS), .out(BrEq), .sel(BrUn));
  Multiplexer multiplexer_2 (.in0(LTU), .in1(LTS), .out(BrLt), .sel(BrUn));

  // Notes on the sheet:
  //   INPUTS to your circuit
  //   DON'T CHANGE THE LOCATIONS OF THE INPUTS AND OUTPUTS!
  //   OUTPUT from your circuit
endmodule
