// Logisim project control-logic.circ as structural Verilog: 1 circuit, main circuit control_logic
module control_logic (
  input  [31:0] Instruction,
  input  BrEq,
  input  BrLt,
  output PCSel,
  output RegWEn,
  output [2:0] ImmSel,
  output BrUn,
  output ASel,
  output BSel,
  output [3:0] ALUSel,
  output MemWEn,
  output [1:0] WBSel
);

  wire BorJ, comparator_37_eq, comparator_38_lt, eight, eighteen, eleven, fifteen, five, four, fourteen,
       nine, nineteen, nonJump, not_1_out, not_2_out, not_3_out, one, priority_encoder_1_gs, Psel26, Psel27,
       Psel28, Psel29, Psel30, Psel31, seven, seventeen, six, sixteen, ten, thirteen, thirty, thirtyfive,
       thirtyfour, thirtyone, thirtythree, thirtytwo, three, twelve, twenty, twentyeight, twentyfive,
       twentyfour, twentynine, twentyone, twentyseven, twentysix, twentythree, twentytwo, two, zero;
  wire [3:0] INDEX2;
  wire [5:0] INDEX;
  wire [15:14] rom_1_data;

  Comparator #(.width(7)) comparator_1 (.a(Instruction[6:0]), .b(7'b0110111), .eq(thirtythree));  // open: gt, lt
  Comparator #(.width(17)) comparator_2 (
    .a({Instruction[6:0], Instruction[14:12], Instruction[31:25]}), .b(17'hcc00), .eq(zero));  // open: gt, lt
  Comparator #(.width(17)) comparator_3 (
    .a({Instruction[6:0], Instruction[14:12], Instruction[31:25]}), .b(17'hcc01), .eq(one));  // open: gt, lt
  Comparator #(.width(17)) comparator_4 (
    .a({Instruction[6:0], Instruction[14:12], Instruction[31:25]}), .b(17'hcc20), .eq(two));  // open: gt, lt
  Comparator #(.width(17)) comparator_5 (
    .a({Instruction[6:0], Instruction[14:12], Instruction[31:25]}), .b(17'hcc80), .eq(three));  // open: gt, lt
  Comparator #(.width(17)) comparator_6 (
    .a({Instruction[6:0], Instruction[14:12], Instruction[31:25]}), .b(17'hcc81), .eq(four));  // open: gt, lt
  Comparator #(.width(17)) comparator_7 (
    .a({Instruction[6:0], Instruction[14:12], Instruction[31:25]}), .b(17'hcd81), .eq(five));  // open: gt, lt
  Comparator #(.width(17)) comparator_8 (
    .a({Instruction[6:0], Instruction[14:12], Instruction[31:25]}), .b(17'hcd00), .eq(six));  // open: gt, lt
  Comparator #(.width(17)) comparator_9 (
    .a({Instruction[6:0], Instruction[14:12], Instruction[31:25]}), .b(17'hce00), .eq(seven));  // open: gt, lt
  Comparator #(.width(17)) comparator_10 (
    .a({Instruction[6:0], Instruction[14:12], Instruction[31:25]}), .b(17'hce80), .eq(eight));  // open: gt, lt
  Comparator #(.width(17)) comparator_11 (
    .a({Instruction[6:0], Instruction[14:12], Instruction[31:25]}), .b(17'hcea0), .eq(nine));  // open: gt, lt
  Comparator #(.width(17)) comparator_12 (
    .a({Instruction[6:0], Instruction[14:12], Instruction[31:25]}), .b(17'hcf00), .eq(ten));  // open: gt, lt
  Comparator #(.width(17)) comparator_13 (
    .a({Instruction[6:0], Instruction[14:12], Instruction[31:25]}), .b(17'hcf80), .eq(eleven));  // open: gt, lt
  Comparator #(.width(10)) comparator_14 (
    .a({Instruction[6:0], Instruction[14:12]}), .b(10'h18), .eq(twelve));  // open: gt, lt
  Comparator #(.width(10)) comparator_15 (
    .a({Instruction[6:0], Instruction[14:12]}), .b(10'h19), .eq(thirteen));  // open: gt, lt
  Comparator #(.width(10)) comparator_16 (
    .a({Instruction[6:0], Instruction[14:12]}), .b(10'h1a), .eq(fourteen));  // open: gt, lt
  Comparator #(.width(10)) comparator_17 (
    .a({Instruction[6:0], Instruction[14:12]}), .b(10'h98), .eq(fifteen));  // open: gt, lt
  Comparator #(.width(17)) comparator_18 (
    .a({Instruction[6:0], Instruction[14:12], Instruction[31:25]}), .b(17'h4c80), .eq(sixteen));  // open: gt, lt
  Comparator #(.width(10)) comparator_19 (
    .a({Instruction[6:0], Instruction[14:12]}), .b(10'h9a), .eq(seventeen));  // open: gt, lt
  Comparator #(.width(10)) comparator_20 (
    .a({Instruction[6:0], Instruction[14:12]}), .b(10'h9c), .eq(eighteen));  // open: gt, lt
  Comparator #(.width(17)) comparator_21 (
    .a({Instruction[6:0], Instruction[14:12], Instruction[31:25]}), .b(17'h4e80), .eq(nineteen));  // open: gt, lt
  Comparator #(.width(17)) comparator_22 (
    .a({Instruction[6:0], Instruction[14:12], Instruction[31:25]}), .b(17'h4ea0), .eq(twenty));  // open: gt, lt
  Comparator #(.width(10)) comparator_23 (
    .a({Instruction[6:0], Instruction[14:12]}), .b(10'h9e), .eq(twentyone));  // open: gt, lt
  Comparator #(.width(10)) comparator_24 (
    .a({Instruction[6:0], Instruction[14:12]}), .b(10'h9f), .eq(twentytwo));  // open: gt, lt
  Comparator #(.width(10)) comparator_25 (
    .a({Instruction[6:0], Instruction[14:12]}), .b(10'h118), .eq(twentythree));  // open: gt, lt
  Comparator #(.width(10)) comparator_26 (
    .a({Instruction[6:0], Instruction[14:12]}), .b(10'h119), .eq(twentyfour));  // open: gt, lt
  Comparator #(.width(10)) comparator_27 (
    .a({Instruction[6:0], Instruction[14:12]}), .b(10'h11a), .eq(twentyfive));  // open: gt, lt
  Comparator #(.width(10)) comparator_28 (
    .a({Instruction[6:0], Instruction[14:12]}), .b(10'h318), .eq(twentysix));  // open: gt, lt
  Comparator #(.width(10)) comparator_29 (
    .a({Instruction[6:0], Instruction[14:12]}), .b(10'h319), .eq(twentyseven));  // open: gt, lt
  Comparator #(.width(10)) comparator_30 (
    .a({Instruction[6:0], Instruction[14:12]}), .b(10'h31c), .eq(twentyeight));  // open: gt, lt
  Comparator #(.width(10)) comparator_31 (
    .a({Instruction[6:0], Instruction[14:12]}), .b(10'h31d), .eq(twentynine));  // open: gt, lt
  Comparator #(.width(10)) comparator_32 (
    .a({Instruction[6:0], Instruction[14:12]}), .b(10'h31e), .eq(thirty));  // open: gt, lt
  Comparator #(.width(10)) comparator_33 (
    .a({Instruction[6:0], Instruction[14:12]}), .b(10'h31f), .eq(thirtyone));  // open: gt, lt
  Comparator #(.width(7)) comparator_34 (.a(Instruction[6:0]), .b(7'b0010111), .eq(thirtytwo));  // open: gt, lt
  Comparator #(.width(7)) comparator_35 (.a(Instruction[6:0]), .b(7'b1101111), .eq(thirtyfour));  // open: gt, lt
  Comparator #(.width(10)) comparator_36 (
    .a({Instruction[6:0], Instruction[14:12]}), .b(10'h338), .eq(thirtyfive));  // open: gt, lt
  ROM #(.addrWidth(6), .dataWidth(16)) rom_1 (
    .addr(INDEX), .data({rom_1_data, WBSel, MemWEn, ALUSel, BSel, ASel, BrUn, ImmSel, RegWEn}));
  Priority_Encoder #(.select_enc(6)) priority_encoder_1 (
    .in0(zero), .in1(one), .in2(two), .in3(three), .in4(four), .in5(five), .in6(six), .in7(seven),
    .in8(eight), .in9(nine), .in10(ten), .in11(eleven), .in12(twelve), .in13(thirteen), .in14(fourteen),
    .in15(fifteen), .in16(sixteen), .in17(seventeen), .in18(eighteen), .in19(nineteen), .in20(twenty),
    .in21(twentyone), .in22(twentytwo), .in23(twentythree), .in24(twentyfour), .in25(twentyfive),
    .in26(twentysix), .in27(twentyseven), .in28(twentyeight), .in29(twentynine), .in30(thirty),
    .in31(thirtyone), .in32(thirtytwo), .in33(thirtythree), .in34(thirtyfour), .in35(thirtyfive),
    .out(INDEX), .gs(priority_encoder_1_gs));  // open: in36, in37, in38, in39, in40, in41, in42, in43, in44, in45, in46, in47, in48, in49, in50, in51, in52, in53, in54, in55, in56, in57, in58, in59, in60, in61, in62, in63, en_out, en_in
  not not_1 (not_1_out, BrLt);
  not not_2 (not_2_out, BrEq);
  not not_3 (not_3_out, BrLt);
  and and_1 (Psel26, twentysix, BrEq);
  and and_2 (Psel27, twentyseven, not_2_out);
  and and_3 (Psel28, twentyeight, BrLt);
  and and_4 (Psel30, thirty, BrLt);
  and and_5 (Psel31, thirtyone, not_1_out);
  and and_6 (Psel29, twentynine, not_3_out);
  Comparator #(.mode("unsigned"), .width(32)) comparator_37 (
    .a(Instruction), .b({32{1'b0}}), .eq(comparator_37_eq));  // open: gt, lt
  Comparator #(.mode("unsigned"), .width(6)) comparator_38 (
    .a(INDEX), .b(6'b011010), .lt(comparator_38_lt));  // open: gt, eq
  or or_1 (nonJump, comparator_37_eq, comparator_38_lt);
  Priority_Encoder #(.select_enc(4)) priority_encoder_2 (
    .in0(twentysix), .in1(twentyseven), .in2(twentyeight), .in3(twentynine), .in4(thirty), .in5(thirtyone),
    .in6(thirtytwo), .in7(thirtythree), .in8(thirtyfour), .in9(thirtyfive), .out(INDEX2));  // open: in10, in11, in12, in13, in14, in15, gs, en_out, en_in
  Multiplexer multiplexer_1 (.in0(BorJ), .in1(1'b0), .out(PCSel), .sel(nonJump));
  Multiplexer #(.select(4)) multiplexer_2 (
    .in0(Psel26), .in1(Psel27), .in2(Psel28), .in3(Psel29), .in4(Psel30), .in5(Psel31), .in6(thirtytwo),
    .in7(1'b0), .in8(thirtyfour), .in9(thirtyfive), .out(BorJ), .sel(INDEX2));  // open: in10, in11, in12, in13, in14, in15

  // Other names for the same wires on the sheet: OP[6:0] = Instruction[6:0];
  //   OPF3[9:0] = {Instruction[6:0], Instruction[14:12]};
  //   OPF3F7[16:0] = {Instruction[6:0], Instruction[14:12], Instruction[31:25]}

  // Notes on the sheet:
  //   INPUTS to your circuit
  //   Connect ROM Input here ->
  //   contents of rom_1 (hex, n*v repeats v):
  //   1005 1405 1605 1085 1485 1585 1105 1205 1285 1685 1305 1385 41 41 41 1041 10c3 1141 1241 12c3 16c3
  //   1341 13c1 846 846 846 4*68 78 78 106b 17cb 206d 2041
  //   ROM FOR CONTROL LOGIC
  //   DON'T CHANGE THE LOCATIONS OF THE INPUTS AND OUTPUTS!
  //   This is only if you choose to do the ROM option
  //   CONNECT
  //   WIRE
  //   TO
  //   USE
  //   ROM
  //   OUTPUT from your circuit
  //   Reminder: If using ROM, use combinational logic for PCSel
endmodule
