// Logisim project cpu.circ as structural Verilog: 1 circuit, main circuit cpu
module cpu (
  input  clk,
  input  [31:0] Instruction,
  input  [31:0] MemReadData,
  output [31:0] MemAddress,
  output [31:0] ProgramCounter,
  output [31:0] ra,
  output [31:0] sp,
  output [31:0] t0,
  output [31:0] t1,
  output [31:0] t2,
  output [31:0] s0,
  output [31:0] s1,
  output [31:0] a0,
  output [3:0] MemWriteMask,
  output [31:0] MemWriteData
);

  wire AS, BE, BL, BS, BU, MWE, partial_store_2_p1, partial_store_2_p2, partial_store_2_p4,
       partial_store_2_p6, PCSel, regfile_1_p1, regfile_1_p2, regfile_1_p4, regfile_1_p6, regfile_1_p8, RWE;
  wire [1:0] WBS;
  wire [2:0] F3, IMMS;
  wire [3:0] control_logic_2_alusel;
  wire [6:0] F7;
  wire [24:0] InstructionTwo;
  wire [31:0] adder_1_out, adder_2_out, DataToReg, IMM, multiplexer_1_out, multiplexer_2_out,
       multiplexer_3_out, multiplexer_4_out, multiplexer_5_out, ProgramCounter2, RD1, RD2;

  Adder #(.width(32)) adder_1 (.a(ProgramCounter), .b(32'h4), .out(adder_1_out));  // open: cin, cout
  Multiplexer #(.width(32)) multiplexer_1 (.in0(adder_1_out), .in1(MemAddress), .out(multiplexer_1_out), .sel(PCSel));
  Multiplexer #(.width(32)) multiplexer_2 (.in0(Instruction), .in1(32'h13), .out(multiplexer_2_out), .sel(PCSel));
  Register #(.width(32)) PC (.D(multiplexer_1_out), .clk(clk), .Q(ProgramCounter));  // open: en, clr
  Register #(.width(32)) register_1 (
    .D(multiplexer_2_out), .clk(clk), .Q({F7, InstructionTwo[24:15], F3, InstructionTwo[11:0]}));  // open: en, clr
  Register #(.width(32)) register_2 (.D(ProgramCounter), .clk(clk), .Q(ProgramCounter2));  // open: en, clr
  // control_logic control_logic_1: pin names not known
  control_logic control_logic_2 (
    .Instruction({F7, InstructionTwo[24:15], F3, InstructionTwo[11:0]}), .BrEq(BE), .BrLt(BL), .PCSel(PCSel),
    .RegWEn(RWE), .ImmSel(IMMS), .BrUn(BU), .ASel(AS), .BSel(BS), .ALUSel(control_logic_2_alusel),
    .MemWEn(MWE), .WBSel(WBS));
  // regfile regfile_1: pin names not known; wires that end beside it: regfile_1_p1, regfile_1_p2, regfile_1_p2, regfile_1_p4, regfile_1_p4, regfile_1_p6, regfile_1_p6, regfile_1_p8, regfile_1_p8
  regfile regfile_2 (
    .ReadIndex1(InstructionTwo[19:15]), .ReadIndex2(InstructionTwo[24:20]),
    .WriteIndex(InstructionTwo[11:7]), .WriteData(multiplexer_5_out), .RegWEn(RWE), .clk(clk), .ra(ra),
    .sp(sp), .t0(t0), .t1(t1), .t2(t2), .s0(s0), .s1(s1), .a0(a0), .ReadData1(RD1), .ReadData2(RD2));
  imm_gen imm_gen_1 (
    .Instruction({F7, InstructionTwo[24:15], F3, InstructionTwo[11:0]}), .ImmSel(IMMS), .Immediate(IMM));
  // imm_gen imm_gen_2: pin names not known
  Multiplexer #(.width(32)) multiplexer_3 (.in0(RD1), .in1(ProgramCounter2), .out(multiplexer_3_out), .sel(AS));
  Multiplexer #(.width(32)) multiplexer_4 (.in0(RD2), .in1(IMM), .out(multiplexer_4_out), .sel(BS));
  alu alu_1 (.A(multiplexer_3_out), .B(multiplexer_4_out), .ALUSel(control_logic_2_alusel), .ALUResult(MemAddress));
  // alu alu_2: pin names not known
  Multiplexer #(.select(2), .width(32)) multiplexer_5 (
    .in0(DataToReg), .in1(MemAddress), .in2(adder_2_out), .out(multiplexer_5_out), .sel(WBS));  // open: in3
  Adder #(.width(32)) adder_2 (.a(32'h4), .b(ProgramCounter2), .out(adder_2_out));  // open: cin, cout
  // branch_comp branch_comp_1: pin names not known
  branch_comp branch_comp_2 (.BrData1(RD1), .BrData2(RD2), .BrUn(BU), .BrEq(BE), .BrLt(BL));
  partial_store partial_store_1 (
    .Instruction({F7, InstructionTwo[24:15], F3, InstructionTwo[11:0]}), .MemAddress(MemAddress),
    .DataFromReg(RD2), .MemWEn(MWE), .MemWriteMask(MemWriteMask), .DataToMem(MemWriteData));
  // partial_store partial_store_2: pin names not known; wires that end beside it: partial_store_2_p1, partial_store_2_p2, partial_store_2_p2, partial_store_2_p4, partial_store_2_p4, partial_store_2_p6, partial_store_2_p1, partial_store_2_p6
  // partial_load partial_load_1: pin names not known
  partial_load partial_load_2 (
    .Instruction({F7, InstructionTwo[24:15], F3, InstructionTwo[11:0]}), .MemAddress(MemAddress),
    .DataFromMem(MemReadData), .DataToReg(DataToReg));

  // Other names for the same wires on the sheet: ALUResult[31:0] = MemAddress; OPC[6:0] = InstructionTwo[6:0];
  //   RD[4:0] = InstructionTwo[11:7]; InstructionTwo (some bits) = {F7, F3}; RI1[4:0] = InstructionTwo[19:15];
  //   RI2[4:0] = InstructionTwo[24:20]

  // Notes on the sheet:
  //   To IMEM
  //   IMEM (do **NOT** move this)
  //   From IMEM
  //   Inputs/Outputs for testing. Do **NOT** move these.
  //   It is OK to move the PC, RegFile, ALU, MEM, Branch Comp, Imm Gen, Partial Load, Partial Store and Control Logic to wherever is most convenient for you when constructing your CPU, and to delete this text
  //   To DMEM
  //   DMEM (do **NOT** move this)
  //   From DMEM
endmodule
