// Logisim project imm-gen.circ as structural Verilog: 1 circuit, main circuit imm_gen
module imm_gen (
  input  [31:0] Instruction,
  input  [2:0] ImmSel,
  output [31:0] Immediate
);

  wire [31:0] typeB, typeI, typeIstar, typeJ, typeS;

  assign typeI = {{20{Instruction[31]}}, Instruction[31:20]};  // Bit_Extender bit_extender_1
  assign typeIstar = {{27{Instruction[24]}}, Instruction[24:20]};  // Bit_Extender bit_extender_2
  assign typeS = {{20{Instruction[31]}}, {Instruction[31:25], Instruction[11:7]}};  // Bit_Extender bit_extender_3
  assign typeB = {{19{Instruction[31]}}, {Instruction[31], Instruction[7], Instruction[30:25], Instruction[11:8], 1'b0}};  // Bit_Extender bit_extender_4
  assign typeJ = {{11{Instruction[31]}}, {Instruction[31], Instruction[19:12], Instruction[20], Instruction[30:21], 1'b0}};  // Bit_Extender bit_extender_5
  Multiplexer #(.select(3), .width(32)) multiplexer_1 (
    .in0(typeI), .in1(typeIstar), .in2(Instruction), .in3(typeS), .in4(typeB),
    .in5({Instruction[31:12], {12{1'b0}}}), .in6(typeJ), .out(Immediate), .sel(ImmSel));  // open: in7

  // Other names for the same wires on the sheet: typeR[31:0] = Instruction; typeU[31:12] = Instruction[31:12]

  // Notes on the sheet:
  //   INPUTS to your circuit
  //   DON'T CHANGE THE LOCATIONS OF THE INPUTS AND OUTPUTS!
  //   OUTPUT from your circuit
endmodule
