// Logisim project partial-load.circ as structural Verilog: 1 circuit, main circuit partial_load
module partial_load (
  input  [31:0] Instruction,
  input  [31:0] MemAddress,
  input  [31:0] DataFromMem,
  output [31:0] DataToReg
);

  wire [7:0] multiplexer_2_out;
  wire [15:0] multiplexer_1_out, undriven;
  wire [31:0] Lb, Lh;

  Multiplexer #(.select(2), .width(16)) multiplexer_1 (
    .in0(DataFromMem[15:0]), .in1(DataFromMem[23:8]), .in2(DataFromMem[31:16]), .in3(undriven),
    .out(multiplexer_1_out), .sel(MemAddress[1:0]));
  assign Lb = {{24{multiplexer_2_out[7]}}, multiplexer_2_out};  // Bit_Extender bit_extender_1
  Multiplexer #(.select(2), .width(8)) multiplexer_2 (
    .in0(DataFromMem[7:0]), .in1(DataFromMem[15:8]), .in2(DataFromMem[23:16]), .in3(DataFromMem[31:24]),
    .out(multiplexer_2_out), .sel(MemAddress[1:0]));
  assign Lh = {{16{multiplexer_1_out[15]}}, multiplexer_1_out};  // Bit_Extender bit_extender_2
  Multiplexer #(.select(2), .width(32)) multiplexer_3 (
    .in0(Lb), .in1(Lh), .in2(DataFromMem), .out(DataToReg), .sel(Instruction[13:12]));  // open: in3

  // Other names for the same wires on the sheet: bottom8[7:0] = DataFromMem[7:0]; bottom16[15:0] = DataFromMem[15:0];
  //   lowermid8[7:0] = DataFromMem[15:8]; middle16[15:0] = DataFromMem[23:8]; upper16[15:0] = DataFromMem[31:16];
  //   uppermid8[7:0] = DataFromMem[23:16]; upper8[7:0] = DataFromMem[31:24]; funct3[1:0] = Instruction[13:12];
  //   MemAdd2[1:0] = MemAddress[1:0]

  // Notes on the sheet:
  //   INPUTS to your circuit
  //   DON'T CHANGE THE LOCATIONS OF THE INPUTS AND OUTPUTS!
  //   OUTPUT from your circuit
endmodule
