// Logisim project partial-store.circ as structural Verilog: 1 circuit, main circuit partial_store
module partial_store (
  input  [31:0] Instruction,
  input  [31:0] MemAddress,
  input  [31:0] DataFromReg,
  input  MemWEn,
  output [3:0] MemWriteMask,
  output [31:0] DataToMem
);

  wire [3:0] multiplexer_3_out, multiplexer_5_out, multiplexer_6_out, multiplexer_7_out;
  wire [31:0] bit_extender_1_out, bit_extender_2_out, bit_extender_3_out, bit_extender_4_out,
       bit_extender_5_out, bit_extender_6_out, multiplexer_1_out, multiplexer_2_out;

  assign bit_extender_1_out = {{16{1'b0}}, DataFromReg[15:0]};  // Bit_Extender bit_extender_1
  assign bit_extender_2_out = {{24{1'b0}}, DataFromReg[7:0]};  // Bit_Extender bit_extender_2
  assign bit_extender_3_out = {{24{1'b0}}, DataFromReg[7:0]};  // Bit_Extender bit_extender_3
  assign bit_extender_4_out = {{16{1'b0}}, DataFromReg[15:0]};  // Bit_Extender bit_extender_4
  assign bit_extender_5_out = {{24{1'b0}}, DataFromReg[7:0]};  // Bit_Extender bit_extender_5
  assign bit_extender_6_out = {{24{1'b0}}, DataFromReg[7:0]};  // Bit_Extender bit_extender_6
  Multiplexer #(.select(2), .width(32)) multiplexer_1 (
    .in0(bit_extender_4_out), .in2({bit_extender_1_out[15:0], bit_extender_1_out[31:16]}),
    .out(multiplexer_1_out), .sel(MemAddress[1:0]));  // open: in1, in3
  Multiplexer #(.select(2), .width(32)) multiplexer_2 (
    .in0(bit_extender_5_out),
    .in1({bit_extender_2_out[31:16], bit_extender_2_out[7:0], bit_extender_2_out[15:8]}),
    .in2({bit_extender_3_out[31:24], bit_extender_3_out[7:0], bit_extender_3_out[23:8]}),
    .in3({bit_extender_6_out[7:0], bit_extender_6_out[31:8]}), .out(multiplexer_2_out), .sel(MemAddress[1:0]));
  Multiplexer #(.select(2), .width(4)) multiplexer_3 (
    .in0(4'b1111), .out(multiplexer_3_out), .sel(MemAddress[1:0]));  // open: in1, in2, in3
  Multiplexer #(.select(2), .width(32)) multiplexer_4 (
    .in0(multiplexer_2_out), .in1(multiplexer_1_out), .in2(DataFromReg), .out(DataToMem),
    .sel(Instruction[13:12]));  // open: in3
  Multiplexer #(.select(2), .width(4)) multiplexer_5 (
    .in0(4'b0001), .in1(4'b0010), .in2(4'b0100), .in3(4'b1000), .out(multiplexer_5_out), .sel(MemAddress[1:0]));
  Multiplexer #(.select(2), .width(4)) multiplexer_6 (
    .in0(4'b0011), .in2(4'b1100), .out(multiplexer_6_out), .sel(MemAddress[1:0]));  // open: in1, in3
  Multiplexer #(.select(2), .width(4)) multiplexer_7 (
    .in0(multiplexer_5_out), .in1(multiplexer_6_out), .in2(multiplexer_3_out), .out(multiplexer_7_out),
    .sel(Instruction[13:12]));  // open: in3
  Multiplexer #(.width(4)) multiplexer_8 (.in0(4'b0000), .in1(multiplexer_7_out), .out(MemWriteMask), .sel(MemWEn));

  // Other names for the same wires on the sheet: Bottom8[7:0] = DataFromReg[7:0]; Bottom16[15:0] = DataFromReg[15:0];
  //   Func3[1:0] = Instruction[13:12]; bottom2[1:0] = MemAddress[1:0]

  // Notes on the sheet:
  //   INPUTS to your circuit
  //   DON'T CHANGE THE LOCATIONS OF THE INPUTS AND OUTPUTS!
  //   OUTPUT from your circuit
endmodule
