// Logisim project regfile.circ as structural Verilog: 1 circuit, main circuit regfile
module regfile (
  input  [4:0] ReadIndex1,
  input  [4:0] ReadIndex2,
  input  [4:0] WriteIndex,
  input  [31:0] WriteData,
  input  RegWEn,
  input  clk,
  output [31:0] ra,
  output [31:0] sp,
  output [31:0] t0,
  output [31:0] t1,
  output [31:0] t2,
  output [31:0] s0,
  output [31:0] s1,
  output [31:0] a0,
  output [31:0] ReadData1,
  output [31:0] ReadData2
);

  wire x0w, x01w, x02w, x03w, x04w, x05w, x06w, x07w, x08w, x09w, x10w, x11w, x12w, x13w, x14w, x15w, x16w,
       x17w, x18w, x19w, x20w, x21w, x22w, x23w, x24w, x25w, x26w, x27w, x28w, x29w, x30w, x31w;
  wire [31:0] x0, x3, x4, x11, x12, x13, x14, x15, x16, x17, x18, x19, x20, x21, x22, x23, x24, x25, x26,
       x27, x28, x29, x30, x31;

  Register #(.width(32)) register_1 (.D(WriteData), .en(x06w), .clk(clk), .Q(t1));  // open: clr
  Register #(.width(32)) register_2 (.D(WriteData), .en(x12w), .clk(clk), .Q(x12));  // open: clr
  Register #(.width(32)) register_3 (.D(WriteData), .en(x18w), .clk(clk), .Q(x18));  // open: clr
  Register #(.width(32)) register_4 (.D(WriteData), .en(x24w), .clk(clk), .Q(x24));  // open: clr
  Register #(.width(32)) register_5 (.D(WriteData), .en(x30w), .clk(clk), .Q(x30));  // open: clr
  Demultiplexer #(.select(5)) demultiplexer_1 (
    .out0(x0w), .out1(x01w), .out2(x02w), .out3(x03w), .out4(x04w), .out5(x05w), .out6(x06w), .out7(x07w),
    .out8(x08w), .out9(x09w), .out10(x10w), .out11(x11w), .out12(x12w), .out13(x13w), .out14(x14w),
    .out15(x15w), .out16(x16w), .out17(x17w), .out18(x18w), .out19(x19w), .out20(x20w), .out21(x21w),
    .out22(x22w), .out23(x23w), .out24(x24w), .out25(x25w), .out26(x26w), .out27(x27w), .out28(x28w),
    .out29(x29w), .out30(x30w), .out31(x31w), .in(RegWEn), .sel(WriteIndex));
  Register #(.width(32)) u_x0 (.D({32{1'b0}}), .en(x0w), .clk(clk), .Q(x0));  // open: clr
  Register #(.width(32)) register_6 (.D(WriteData), .en(x01w), .clk(clk), .Q(ra));  // open: clr
  Register #(.width(32)) register_7 (.D(WriteData), .en(x07w), .clk(clk), .Q(t2));  // open: clr
  Register #(.width(32)) register_8 (.D(WriteData), .en(x13w), .clk(clk), .Q(x13));  // open: clr
  Register #(.width(32)) register_9 (.D(WriteData), .en(x19w), .clk(clk), .Q(x19));  // open: clr
  Register #(.width(32)) register_10 (.D(WriteData), .en(x25w), .clk(clk), .Q(x25));  // open: clr
  Register #(.width(32)) register_11 (.D(WriteData), .en(x31w), .clk(clk), .Q(x31));  // open: clr
  Register #(.width(32)) register_12 (.D(WriteData), .en(x08w), .clk(clk), .Q(s0));  // open: clr
  Register #(.width(32)) register_13 (.D(WriteData), .en(x14w), .clk(clk), .Q(x14));  // open: clr
  Register #(.width(32)) register_14 (.D(WriteData), .en(x20w), .clk(clk), .Q(x20));  // open: clr
  Register #(.width(32)) register_15 (.D(WriteData), .en(x26w), .clk(clk), .Q(x26));  // open: clr
  Register #(.width(32)) register_16 (.D(WriteData), .en(x02w), .clk(clk), .Q(sp));  // open: clr
  Multiplexer #(.select(5), .width(32)) multiplexer_1 (
    .in0(x0), .in1(ra), .in2(sp), .in3(x3), .in4(x4), .in5(t0), .in6(t1), .in7(t2), .in8(s0), .in9(s1),
    .in10(a0), .in11(x11), .in12(x12), .in13(x13), .in14(x14), .in15(x15), .in16(x16), .in17(x17),
    .in18(x18), .in19(x19), .in20(x20), .in21(x21), .in22(x22), .in23(x23), .in24(x24), .in25(x25),
    .in26(x26), .in27(x27), .in28(x28), .in29(x29), .in30(x30), .in31(x31), .out(ReadData1), .sel(ReadIndex1));
  Register #(.width(32)) register_17 (.D(WriteData), .en(x03w), .clk(clk), .Q(x3));  // open: clr
  Register #(.width(32)) register_18 (.D(WriteData), .en(x09w), .clk(clk), .Q(s1));  // open: clr
  Register #(.width(32)) register_19 (.D(WriteData), .en(x15w), .clk(clk), .Q(x15));  // open: clr
  Register #(.width(32)) register_20 (.D(WriteData), .en(x21w), .clk(clk), .Q(x21));  // open: clr
  Register #(.width(32)) register_21 (.D(WriteData), .en(x27w), .clk(clk), .Q(x27));  // open: clr
  Register #(.width(32)) register_22 (.D(WriteData), .en(x04w), .clk(clk), .Q(x4));  // open: clr
  Register #(.width(32)) register_23 (.D(WriteData), .en(x10w), .clk(clk), .Q(a0));  // open: clr
  Register #(.width(32)) register_24 (.D(WriteData), .en(x16w), .clk(clk), .Q(x16));  // open: clr
  Register #(.width(32)) register_25 (.D(WriteData), .en(x22w), .clk(clk), .Q(x22));  // open: clr
  Register #(.width(32)) register_26 (.D(WriteData), .en(x28w), .clk(clk), .Q(x28));  // open: clr
  Register #(.width(32)) register_27 (.D(WriteData), .en(x17w), .clk(clk), .Q(x17));  // open: clr
  Register #(.width(32)) register_28 (.D(WriteData), .en(x23w), .clk(clk), .Q(x23));  // open: clr
  Register #(.width(32)) register_29 (.D(WriteData), .en(x29w), .clk(clk), .Q(x29));  // open: clr
  Register #(.width(32)) register_30 (.D(WriteData), .en(x05w), .clk(clk), .Q(t0));  // open: clr
  Register #(.width(32)) register_31 (.D(WriteData), .en(x11w), .clk(clk), .Q(x11));  // open: clr
  Multiplexer #(.select(5), .width(32)) multiplexer_2 (
    .in0(x0), .in1(ra), .in2(sp), .in3(x3), .in4(x4), .in5(t0), .in6(t1), .in7(t2), .in8(s0), .in9(s1),
    .in10(a0), .in11(x11), .in12(x12), .in13(x13), .in14(x14), .in15(x15), .in16(x16), .in17(x17),
    .in18(x18), .in19(x19), .in20(x20), .in21(x21), .in22(x22), .in23(x23), .in24(x24), .in25(x25),
    .in26(x26), .in27(x27), .in28(x28), .in29(x29), .in30(x30), .in31(x31), .out(ReadData2), .sel(ReadIndex2));

  // Other names for the same wires on the sheet: WD[31:0] = WriteData; x1[31:0] = ra; x2[31:0] = sp; x5[31:0] = t0;
  //   x6[31:0] = t1; x7[31:0] = t2; x8[31:0] = s0; x9[31:0] = s1; x10[31:0] = a0

  // Notes on the sheet:
  //   INPUTS to your circuit
  //   DON'T CHANGE THE LOCATIONS OF THE INPUTS AND OUTPUTS!
  //   These are DEBUG/TEST outputs from your circuit.
  //   OUTPUTS from your circuit
endmodule
